# Fritzing sketch EmbRotary_Circuit (saved by Fritzing 1.0.6)
circuit board: 6.97739cm x 7.14443cm
breadboards: 1

parts:
  J1 = Dagu DGServo 9g header (male) [package=THT]
  J2 = Dagu DGServo 9g header (male) [package=THT]
  J3 = Dagu DGServo 9g header (male) [package=THT]
  C1 = Electrolytic Capacitor [capacitance=0.1mF voltage=35V package="100 mil [THT, electrolytic]"]
  C2 = Electrolytic Capacitor [capacitance=0.1mF voltage=35V package="100 mil [THT, electrolytic]"]
  C3 = Electrolytic Capacitor [capacitance=0.1mF voltage=35V package="100 mil [THT, electrolytic]"]
  C4 = Electrolytic Capacitor [capacitance=0.1mF voltage=35V package="100 mil [THT, electrolytic]"]
  C5 = Ceramic Capacitor [capacitance=100nF voltage=35V package="100 mil [THT, multilayer]"]
  C6 = Ceramic Capacitor [capacitance=100nF voltage=35V package="100 mil [THT, multilayer]"]
  C7 = Ceramic Capacitor [capacitance=100nF voltage=35V package="100 mil [THT, multilayer]"]
  D1 = Schottky Diode [part_number=1N5819 package="300 mil [THT]"]
  C8 = Electrolytic Capacitor [capacitance=1mF voltage=35V package="100 mil [THT, electrolytic]"]
  D2 = Rectifier Diode [part_number=P6KE5.0A package="300 mil [THT]"]
  V1 = DC Power Supply [voltage=5V internal_resistance=1Ω max_current=3A]
  R1 = Rotary Potentiometer (Large) [maximum_resistance=10kΩ knob_status=50% power=0.5W package=THT]
  R2 = Rotary Potentiometer (Large) [maximum_resistance=10kΩ knob_status=50% power=0.5W package=THT]
  R3 = Rotary Potentiometer (Large) [maximum_resistance=10kΩ knob_status=50% power=0.5W package=THT]
  R4 = Resistor [tolerance=±5% power=0.25W resistance=1k package=THT]
  R5 = Resistor [tolerance=±5% power=0.25W resistance=1k package=THT]
  R6 = Resistor [tolerance=±5% power=0.25W resistance=1k package=THT]
  D3 = Rectifier Diode [part_number=1N4001 package="300 mil [THT]"]
  D4 = Rectifier Diode [part_number=1N4001 package="300 mil [THT]"]
  D5 = Rectifier Diode [part_number=1N4001 package="300 mil [THT]"]
  Mod1 = Raspberry Pi Pico

nets (from the schematic view):
  GND: J1.gnd, J2.gnd, J3.gnd, C1.-, C2.-, C3.-, C4.-, C5.0, C6.0, C7.0, C8.-, D2.anode, V1.Pin_1, R1.leg2, R2.leg2, R3.leg2, D3.anode, D4.anode, D5.anode, Mod1.pin_3, Mod1.pin_8, Mod1.pin_13, Mod1.pin_18, Mod1.pin_23, Mod1.pin_28, Mod1.pin_33, Mod1.pin_38, Mod1.pin_42
  VCC: J1.Vcc, J2.Vcc, J3.Vcc, C1.+, C2.+, C3.+, C4.+, C5.1, C6.1, C7.1, D1.cathode, C8.+, D2.cathode, Mod1.pin_39
  N1: J1.pulse, Mod1.pin_1
  N2: J2.pulse, Mod1.pin_4
  N3: J3.pulse, Mod1.pin_6
  N4: D1.anode, V1.Pin_2
  N5: R1.leg1, R2.leg1, R3.leg1, Mod1.pin_36
  N6: R1.wiper, R4.Pin_0
  N7: R2.wiper, R5.Pin_0
  N8: R3.wiper, R6.Pin_0
  N9: R4.Pin_1, D3.cathode, Mod1.pin_31
  N10: R5.Pin_1, D4.cathode, Mod1.pin_32
  N11: R6.Pin_1, D5.cathode, Mod1.pin_34

custom parts:
  Raspberry Pi Pico: Raspberry Pi Pico. Based around the RP2040 microcontroller the Pico is a low cost microcontroller device bringing Raspberry Pi quality, cost, and easy of use to the microcontroller space. Jan 2021, Split part in to two versions: tht (this one) and SMD. This one will drill holes for a .1 in header in pcb to allow plugging in the module as well as providing pads to solder the module to the top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
